# Fritzing sketch Hardware_sketch_Fritzing (saved by Fritzing 0.9.2b)

parts:
  Bauteil1 = Adafruit Feather M0 Adalogger [part_number="Adafruit #2796"]
  BC127_Dev1 = SparkFun Purpletooth Jamboree - BC127 Development Board
  Bauteil3 = Adafruit I2S Mic - SPH0645 [part_number="Adafruit #3421"]
  Bauteil4 = Adafruit I2S Mic - SPH0645 [part_number="Adafruit #3421"]

nets:
  GND: Bauteil1.GND, BC127_Dev1.GND, Bauteil3.GND, Bauteil4.GND, Bauteil4.SELECT
  N1: Bauteil1.D1, Bauteil3.BCLK, Bauteil4.BCLK
  N2: Bauteil1.D0, Bauteil3.WS, Bauteil4.WS
  VDD: Bauteil1.+3V3, Bauteil3.VDD, Bauteil3.SELECT, Bauteil4.VDD
  N3: Bauteil1.D11, BC127_Dev1.TXO
  N4: Bauteil1.D10, BC127_Dev1.RXI
  N5: Bauteil1.D9, Bauteil3.DATA, Bauteil4.DATA
  N6: Bauteil1.SDA, BC127_Dev1.!RESET

custom parts:
  Adafruit Feather M0 Adalogger: This is the Adafruit Feather M0 Adalogger - our take on an 'all-in-one' Cortex M0 datalogger (or data-reader) with built in USB and battery charging. Its an Adafruit Feather M0 with a microSD holder ready to rock! We have other boards in the Feather family, check'em out here At the Feather M0's heart is an ATSAMD21G18 ARM Cortex M0 processor, clocked at 48 MHz and at 3.3V logic, the same one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
  SparkFun Purpletooth Jamboree - BC127 Development Board: This is the PurpleTooth Jamboree a full-function board, designed to provide audio bridge support through the A2DP, HFP, and AVRCP Bluetooth Classic profiles. The module is also dual mode which means it can operate as Bluetooth 2.1 or Bluetooth 4.0 (BLE). It includes circuitry for converting single-ended audio inputs and microphones to balanced inputs for the module, and converting the module’s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
  Adafruit I2S Mic - SPH0645: For many microcontrollers, adding audio input is easy with one of our analog microphone breakouts. But as you get to bigger and better microcontrollers and microcomputers, you'll find that you don't always have an analog input, or maybe you want to avoid the noise that can seep in with an analog mic system. Once you get past 8-bit micros, you will often find an I2S peripheral, that can take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
